# Fritzing sketch 555LedBlink (saved by Fritzing 0.9.3b)
circuit board: 6.92386cm x 3.86289cm
breadboards: 1

parts:
  U1_555_IC = 555 Timer [package="DIP8 [THT]"]
  VCC1_9V_Batt = Battery block 9V
  R1_1k = Resistor [tolerance=±5% resistance=1k package=THT]
  LED1 = LED - 5mm [color="Yellow (592nm)" package="5 mm [THT]"]
  C1_1uF = Electrolytic Capacitor [capacitance=1µF package="100 mil [THT, electrolytic]"]
  R2_470k = Resistor [tolerance=±5% resistance=470k package=THT]
  R3_1k = Resistor [tolerance=±5% resistance=1k package=THT]

nets:
  N1: U1_555_IC.Pin_1, VCC1_9V_Batt.-, LED1.cathode, C1_1uF.-
  N2: U1_555_IC.Pin_2, U1_555_IC.Pin_6, C1_1uF.+, R2_470k.Pin_0
  N3: U1_555_IC.Pin_3, R1_1k.Pin_0
  N4: U1_555_IC.Pin_4, U1_555_IC.Pin_8, VCC1_9V_Batt.+, R3_1k.Pin_1
  N5: U1_555_IC.Pin_7, R2_470k.Pin_1, R3_1k.Pin_0
  N6: R1_1k.Pin_1, LED1.anode
